# Fritzing sketch Robot Schematic (saved by Fritzing 0.9.10b)
circuit board: 6.39743cm x 9.45691cm
breadboards: 1

parts:
  P1 = Arduino Nano (Rev3.0)
  M1 = DC Motor [voltage_(max)=6V voltage_(min)=3V]
  P3 = Motor Driver 1A Dual TB6612FNG
  LED1 = LEDs [package=led10mm]
  U1 = Voltage Regulator - 5V [package="TO220 [THT]"]
  C1 = Capacitor Polarized [package=cpol-radial-100uf-25v]
  C2 = Capacitor Polarized [package=cpol-radial-100uf-25v]
  C3 = Capacitor Polarized [package=cpol-radial-100uf-25v]
  P2 = NRF24L01+ Breakout Board
  J1 = Basic Servo
  R1 = Resistor [tolerance=±5% resistance=220 power=0W package="2512 [SMD]"]
  U2 = Voltage Regulator - 3.3V [package="TO220 [THT]"]
  VCC1 = Battery block 9V

nets:
  GND: P1.GND, P3.GND, U1.GND, C1.-, C2.-, C3.-, P2.GND, J1.gnd, R1.Pin_1, U2.GND, VCC1.-
  N1: P1.D2, P3.STBY
  N2: P1.D3, P3.PWMA
  N3: P1.D4, P3.AIN2
  N4: P1.D5, P3.AIN1
  N5: P1.D6, LED1.A
  N6: P1.D7, P2.CE
  N7: P1.D8, P2.CS
  N8: P1.D9, J1.pulse
  N9: P1.D11/MOSI, P2.MOSI
  N10: P1.D12/MISO, P2.MISO
  VCC: P1.VIN, P3.VCC, P3.VM, U1.output_voltage, C1.+, J1.vcc
  N11: P1.D13/SCK, P2.SCK
  N12: M1.pin_1, P3.A01
  N13: M1.pin_2, P3.A02
  N14: LED1.C, R1.Pin_0
  N15: U1.input_voltage, C3.+, U2.input_voltage, VCC1.+
  N16: C2.+, P2.VCC, U2.output_voltage

notes:
  - U1: 7805 - 5V regulator
  - U2: 7833 - 3.3V regulator
  - C1: 100uf eletrolytic capacitor
  - C2: 100uf eletrolytic capacitor
  - C3: 100uf eletrolytic capacitor
  - M1: 6v motor
  - J1: Micro servo motor 9g SG90
  - LED1: Green LED
  - R1: 220 Ohms resistor
  - P1: Arduino Nano
  - P2: NRF24L01+
  - P3: TB6612FNG - dual H bridge
